# Fritzing sketch lcd (saved by Fritzing 0.9.3b)
breadboards: 1

parts:
  ODROID_C1 = ODROID C2
  U1 = LCD-16X2 [package=lcd-16x2]
  R1 = Rotary Potentiometer (Large) [maximum_resistance=1kΩ package=THT]
  R2 = Resistor [tolerance=±5% resistance=680 package="2010 [SMD]"]

nets:
  N1: ODROID_C1.249, U1.RS
  N2: ODROID_C1.247, U1.E
  N3: ODROID_C1.239, U1.DB4
  N4: ODROID_C1.237, U1.DB5
  N5: ODROID_C1.236, U1.DB7
  N6: ODROID_C1.238, U1.DB6
  N7: ODROID_C1.GND, U1.R_W, U1.K, R1.leg1, R1.leg2
  5V: ODROID_C1.5V, U1.VSS, U1.VDD, R2.Pin_1
  N8: U1.VO, R1.wiper

custom parts:
  ODROID C2: The ODROID-C2 is a 64-bit quad-core single board computer(SBC) that is one of the most cost-effective 64bit development boards available in the ARM world. It can function as a home theater set-top box, a general purpose computer for web browsing, gaming and socializing, a compact tool for college or office work, a prototyping device for hardware tinkering, a controller for home automation, a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
